# Fritzing sketch alarma prototipo 1 (saved by Fritzing 0.9.0b)
breadboards: 1

parts:
  IC1 = DIP - 14 pins [chip_label=74LS11 package="DIP (Dual Inline) [THT]"]
  U1 = 74HC4051 [package=so16]
  Parte1 = Arduino Leonardo (Rev3b)
  B2 = Pushbutton [package="[THT]"]
  R1 = Resistor [tolerance=±5% resistance=220 package=THT]
  B1 = Pushbutton [package="[THT]"]
  R2 = Resistor [tolerance=±5% resistance=220 package=THT]
  B3 = Pushbutton [package="[THT]"]
  R3 = Resistor [tolerance=±5% resistance=220 package=THT]
  LED1 = smd LED [color="Red (633nm)" package="1206 [SMD]"]

nets:
  GND: IC1.GND, U1.INH, U1.VEE, U1.VSS, Parte1.GND, B2.Pin_3, B2.Pin_4, B1.Pin_4, B3.Pin_3, B3.Pin_4, LED1.cathode
  N1: IC1.Y3, Parte1.D0/RX
  N2: IC1.A3, U1.IO3, B3.Pin_1, B3.Pin_2, R3.Pin_1
  N3: IC1.B3, U1.IO2, B2.Pin_1, B2.Pin_2, R1.Pin_1
  N4: IC1.C3, U1.IO1, B1.Pin_2, R2.Pin_1
  VCC: IC1.VCC, U1.VDD, Parte1.5V, R1.Pin_0, R2.Pin_0, R3.Pin_0
  N5: U1.IO, Parte1.D9_PWM/A9
  N6: U1.C, Parte1.D5_PWM
  N7: U1.B, Parte1.D4/A6
  N8: U1.A, Parte1.D3_PWM/SCL
  N9: Parte1.D2/SDA, Parte1.SDA
  N10: Parte1.D13_PWM, LED1.anode

custom parts:
  DIP - 14 pins: A DIP stand-in part for whatever IC you want. With 14 pins on a 300mil dual inline package (DIP) footprint.
